// Logisim project 作业3.circ as structural Verilog: 1 circuit, main circuit main
module main (
  input  I0,
  input  I1,
  input  I2,
  input  I3,
  input  I4,
  input  I5,
  input  I6,
  output ALUSRC,
  output MemtoReg,
  output RegWrite,
  output MemRead,
  output Memwrite,
  output Branch,
  output ALUOp1,
  output ALUOp0
);

  wire not_1_out, not_2_out, not_3_out, not_4_out, not_5_out, not_6_out, not_7_out;

  not not_1 (not_1_out, I1);
  not not_2 (not_2_out, I0);
  not not_3 (not_3_out, I3);
  not not_4 (not_4_out, I2);
  not not_5 (not_5_out, I4);
  not not_6 (not_6_out, I6);
  not not_7 (not_7_out, I5);
  and and_1 (ALUOp1, I0, I1, not_4_out, not_3_out, I4, I5, not_6_out);
  and and_2 (MemRead, I0, I1, not_4_out, not_3_out, not_5_out, not_7_out, not_6_out);
  and and_3 (Memwrite, I0, I1, not_4_out, not_3_out, not_5_out, I5, not_6_out);
  and and_4 (ALUOp0, I0, I1, not_4_out, not_3_out, not_5_out, I5, I6);
  or or_1 (ALUSRC, MemRead, Memwrite);
  or or_2 (RegWrite, ALUOp1, MemRead);

  assign Branch = ALUOp0;
  assign MemtoReg = MemRead;
endmodule
